# Fritzing sketch electrical_layout (saved by Fritzing 1.0.6)

parts:
  U1 = ESP32S-HiLetgo [part_number=ESP32S-HiLetgo]
  A1 = Raspberry Pi 5
  BAT3 = Battery Holders [package=lipo-1100mAh]
  BAT2 = Battery Holders [package=lipo-1100mAh]
  BAT1 = Battery Holders [package=lipo-1100mAh]
  Mod1 = 3S-BMS
  M1 = DC Motor [voltage_(max)=24V voltage_(min)=3V]
  M2 = DC Motor [voltage_(max)=24V voltage_(min)=3V]
  Stepdown_Voltage1 = Polulu Stepdown Voltage [part_number=D24V25F3,D24V25F5]
  A2 = Dual VNH2SP30 Motor Driver [part_number=MD03A]

nets:
  N1: U1.GPIO32, A2.Pin_4
  N2: U1.GPIO33, A2.Pin_12
  N3: U1.GPIO25, A2.Pin_2
  N4: U1.GPIO26, A2.Pin_3
  N5: U1.GPIO27, A2.Pin_14
  N6: U1.GPIO14, A2.Pin_13
  N7: U1.GPIO12, A2.Pin_1, A2.Pin_15
  N8: U1.GND, A1.PWR-1, Stepdown_Voltage1.GND#3
  N9: U1.GPIO9, A1.GPIO14
  N10: U1.GPIO10, A1.GPIO15
  N11: U1.VIN, A1.PWR-2, Stepdown_Voltage1.VOut
  N12: BAT3.+, BAT2.-, Mod1.8.4V
  N13: BAT3.-, Mod1.12.6V
  N14: BAT2.+, BAT1.-, Mod1.4.2V
  N15: BAT1.+, Mod1.0V
  N16: Mod1.-, Stepdown_Voltage1.GND#2, A2.Pin_9, A2.pin_19
  N17: Mod1.+, Stepdown_Voltage1.VIn, A2.Pin_6, A2.Pin_18
  N18: M1.pin_1, A2.Pin_17
  N19: M1.pin_2, A2.Pin_16
  N20: M2.pin_1, A2.Pin_21
  N21: M2.pin_2, A2.Pin_20

custom parts:
  ESP32S-HiLetgo: HiLetgo ESP-WROOM-32 ESP32 ESP-32S Development Board 2.4GHz Dual-Mode WiFi + Bluetooth Dual Cores Microcontroller The ESP32 integrated with Antenna switches, RF Balun, power amplifiers, low-noise amplifiers, filters, and management modules, and the entire solution occupies the least area of PCB. 2.4 GHz Wi-Fi plus Bluetooth dual-mode chip, with TSMC Ultra-low power consumption 40nm technology,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
  Raspberry Pi 5: The RPi5, a faster version of the awesome Raspberry Pi4B ARM Board with 40 pin gpio.
  3S-BMS: 3S-BMS LIPO battery charger / protection unit. Note pcb does not match the board as it will likely connect with wires, so pcb is 6 pads suitable for .1in header pins.
  Polulu Stepdown Voltage: Polulu Stepdown Voltage 3V3 or 5V, 2.5A
